# Fritzing sketch NodeMCU_LDR (saved by Fritzing 0.9.3b)
breadboards: 1

parts:
  R1 = Resistor [tolerance=±5% resistance=10k package=THT]
  R2 = Photocell (LDR) [package=THT]
  U1 = NodeMCU V3.0

nets:
  N1: R1.Pin_0, R2.pin_1, U1.A0
  N2: R1.Pin_1, U1.GND#6, U1.GND#13, U1.GND#16, U1.GND#33
  N3: R2.pin_0, U1.3V3

custom parts:
  NodeMCU V3.0: ESP8266 based NodeMCU
